// Logisim project main.circ as structural Verilog: 18 circuits, main circuit main
module main (
  input  RESET
);

  wire clock_1_out, cpu_1_fetch, cpu_1_mem_read, cpu_1_mem_write, n7segdisplay_selector_1_a,
       n7segdisplay_selector_1_b, n7segdisplay_selector_1_c, n7segdisplay_selector_1_d,
       n7segdisplay_selector_1_e, n7segdisplay_selector_1_f, n7segdisplay_selector_1_g,
       n7segdisplay_selector_2_a, n7segdisplay_selector_2_b, n7segdisplay_selector_2_c,
       n7segdisplay_selector_2_d, n7segdisplay_selector_2_e, n7segdisplay_selector_2_f,
       n7segdisplay_selector_2_g;
  wire [3:0] cpu_1_ad_out, cpu_1_data_out, cpu_1_pc_out, ram_1_data;
  wire [11:0] rom_1_data;

  _7_Segment_Display u_7_segment_display_1 (
    .g(n7segdisplay_selector_1_g), .f(n7segdisplay_selector_1_f), .a(n7segdisplay_selector_1_a),
    .b(n7segdisplay_selector_1_b), .e(n7segdisplay_selector_1_e), .d(n7segdisplay_selector_1_d),
    .c(n7segdisplay_selector_1_c));  // open: dp
  _7SegDisplay_Selector u_7segdisplay_selector_1 (
    .in_1(cpu_1_pc_out), .a(n7segdisplay_selector_1_a), .b(n7segdisplay_selector_1_b),
    .c(n7segdisplay_selector_1_c), .d(n7segdisplay_selector_1_d), .e(n7segdisplay_selector_1_e),
    .f(n7segdisplay_selector_1_f), .g(n7segdisplay_selector_1_g));
  ROM #(.addrWidth(4), .dataWidth(12)) rom_1 (.addr(cpu_1_pc_out), .data(rom_1_data), .sel(cpu_1_fetch));
  Clock clock_1 (.out(clock_1_out));
  CPU cpu_1 (
    .CLK(clock_1_out), .RI_in(rom_1_data), .RESET(RESET), .fetch(cpu_1_fetch), .MEM_read(cpu_1_mem_read),
    .MEM_write(cpu_1_mem_write), .DATA_in(ram_1_data), .DATA_out(cpu_1_data_out), .AD_out(cpu_1_ad_out),
    .PC_out(cpu_1_pc_out));  // open: ext1, ext2
  RAM #(.addrWidth(4), .dataWidth(4), .bus("separate")) ram_1 (
    .addr(cpu_1_ad_out), .din(cpu_1_data_out), .data(ram_1_data), .str(cpu_1_mem_write), .clk(clock_1_out),
    .ld(cpu_1_mem_read), .clr(RESET));  // open: sel
  _7_Segment_Display u_7_segment_display_2 (
    .g(n7segdisplay_selector_2_g), .f(n7segdisplay_selector_2_f), .a(n7segdisplay_selector_2_a),
    .b(n7segdisplay_selector_2_b), .e(n7segdisplay_selector_2_e), .d(n7segdisplay_selector_2_d),
    .c(n7segdisplay_selector_2_c));  // open: dp
  _7SegDisplay_Selector u_7segdisplay_selector_2 (
    .in_1(cpu_1_data_out), .a(n7segdisplay_selector_2_a), .b(n7segdisplay_selector_2_b),
    .c(n7segdisplay_selector_2_c), .d(n7segdisplay_selector_2_d), .e(n7segdisplay_selector_2_e),
    .f(n7segdisplay_selector_2_f), .g(n7segdisplay_selector_2_g));

  // Notes on the sheet:
  //   contents of rom_1 (hex, n*v repeats v):
  //   400 444 384 888 184 88c 284 890 84 894 7c4 8d8
endmodule

module XOR (
  input  A,
  input  B,
  output S
);

  wire and_1_out, and_2_out;

  and and_1 (and_1_out, ~A, B);  // AND_Gate
  and and_2 (and_2_out, A, ~B);  // AND_Gate
  or or_1 (S, and_1_out, and_2_out);
endmodule

module Half_Adder (
  input  A,
  input  B,
  output S,
  output R
);

  and and_1 (R, A, B);
  XOR xor_1 (.A(A), .S(S), .B(B));
endmodule

module MUX (
  input  e1,
  input  e0,
  input  sel,
  output s
);

  wire and_1_out, and_2_out, not_1_out;

  not not_1 (not_1_out, sel);
  and and_1 (and_1_out, e1, sel);
  and and_2 (and_2_out, e0, not_1_out);
  or or_1 (s, and_1_out, and_2_out);
endmodule

module Full_Adder (
  input  Carry_in,
  input  A,
  input  B,
  output Sum,
  output Carry_out
);

  wire and_1_out, and_2_out, xor_1_out;

  and and_1 (and_1_out, A, B);
  xor xor_1 (xor_1_out, A, B);
  or or_1 (Carry_out, and_1_out, and_2_out);
  and and_2 (and_2_out, xor_1_out, Carry_in);
  xor xor_2 (Sum, Carry_in, xor_1_out);
endmodule

module DEC (
  input  e2,
  input  e1,
  input  e0,
  output D0,
  output D1,
  output D2,
  output D3,
  output D4,
  output D5,
  output D6,
  output D7
);

  wire not_1_out, not_2_out, not_3_out;

  not not_1 (not_1_out, e2);
  not not_2 (not_2_out, e1);
  not not_3 (not_3_out, e0);
  and and_1 (D0, not_1_out, not_2_out, not_3_out);
  and and_2 (D1, not_1_out, not_2_out, e0);
  and and_3 (D2, not_1_out, e1, not_3_out);
  and and_4 (D3, not_1_out, e1, e0);
  and and_5 (D4, e2, not_2_out, not_3_out);
  and and_6 (D5, e2, not_2_out, e0);
  and and_7 (D6, e2, e1, not_3_out);
  and and_8 (D7, e2, e1, e0);
endmodule

module LogicalUnit (
  input  A,
  input  B,
  output AND,
  output OR,
  output NOT
);

  and u_AND (AND, A, B);
  or u_OR (OR, A, B);
  not not_1 (NOT, B);
endmodule

module ALU_2 (
  input  Cin,
  input  A,
  input  B,
  input  F2,
  input  F1,
  input  F0,
  output S,
  output Cout
);

  wire and_1_out, and_2_out, and_3_out, and_4_out, dec_1_d0, dec_1_d1, dec_1_d2, dec_1_d3, dec_1_d7,
       full_adder_1_sum, inverter_1_s, logicalunit_1_and, logicalunit_1_not, logicalunit_1_or, or_1_out;

  LogicalUnit logicalunit_1 (.A(A), .B(B), .AND(logicalunit_1_and), .OR(logicalunit_1_or), .NOT(logicalunit_1_not));
  DEC dec_1 (
    .e2(F2), .e1(F1), .e0(F0), .D0(dec_1_d0), .D1(dec_1_d1), .D2(dec_1_d2), .D3(dec_1_d3), .D7(dec_1_d7));  // open: D4, D5, D6
  Inverter inverter_1 (.E(B), .S(inverter_1_s), .Sel(dec_1_d7));
  Full_Adder full_adder_1 (.A(A), .B(inverter_1_s), .Sum(full_adder_1_sum), .Carry_in(Cin), .Carry_out(Cout));
  or or_1 (or_1_out, dec_1_d0, dec_1_d7);
  and and_1 (and_1_out, logicalunit_1_and, dec_1_d2);
  and and_2 (and_2_out, logicalunit_1_or, dec_1_d1);
  and and_3 (and_3_out, logicalunit_1_not, dec_1_d3);
  and and_4 (and_4_out, full_adder_1_sum, or_1_out);
  or OR4 (S, and_1_out, and_2_out, and_3_out, and_4_out);
endmodule

module Inverter (
  input  E,
  input  Sel,
  output S
);

  wire and_1_out, and_2_out, not_1_out;

  not not_1 (not_1_out, E);
  and and_1 (and_1_out, E, ~Sel);  // AND_Gate
  and and_2 (and_2_out, not_1_out, Sel);
  xor xor_1 (S, and_1_out, and_2_out);
endmodule

module _4bits_ALU (
  input  F2,
  input  F1,
  input  in_3,
  input  [3:0] A,
  input  [3:0] B,
  input  ext1,
  input  ext2,
  output out_8,
  output [3:0] S
);

  wire alu_2_2_cout, alu_2_3_cout, alu_2_4_cout, and_2_out;

  and and_1 (out_8, ~S[0], ~S[1], ~S[2], ~S[3]);  // AND_Gate
  ALU_2 alu_2_1 (.A(A[3]), .B(B[3]), .F2(F2), .F1(F1), .F0(in_3), .S(S[3]), .Cin(alu_2_2_cout));  // open: Cout
  ALU_2 alu_2_2 (.A(A[2]), .B(B[2]), .F2(F2), .F1(F1), .F0(in_3), .S(S[2]), .Cin(alu_2_3_cout), .Cout(alu_2_2_cout));
  ALU_2 alu_2_3 (.A(A[1]), .B(B[1]), .F2(F2), .F1(F1), .F0(in_3), .S(S[1]), .Cin(alu_2_4_cout), .Cout(alu_2_3_cout));
  ALU_2 alu_2_4 (.A(A[0]), .B(B[0]), .F2(F2), .F1(F1), .F0(in_3), .S(S[0]), .Cin(and_2_out), .Cout(alu_2_4_cout));
  and and_2 (and_2_out, F2, F1, in_3);

  // Other names for the same wires on the sheet: F0 = in_3

  // Notes on the sheet:
  //   Instructions:
  //   000 : ADD
  //   001: OR
  //   010: AND
  //   011: NOT
  //   111: SUB
  //   SUB
endmodule

module _4bitsRegister (
  input  [3:0] R,
  input  w,
  input  CK,
  input  r_2,
  input  r2,
  output [3:0] Y,
  output [3:0] X
);

  wire controlled_buffer_1_out, controlled_buffer_2_out, controlled_buffer_3_out, controlled_buffer_4_out,
       d_ff_1_q, d_ff_2_q, d_ff_3_q, d_ff_4_q;

  assign controlled_buffer_1_out = w ? R[2] : 1'bz;  // Controlled_Buffer controlled_buffer_1
  assign controlled_buffer_2_out = w ? R[3] : 1'bz;  // Controlled_Buffer controlled_buffer_2
  assign controlled_buffer_3_out = w ? R[0] : 1'bz;  // Controlled_Buffer controlled_buffer_3
  assign controlled_buffer_4_out = w ? R[1] : 1'bz;  // Controlled_Buffer controlled_buffer_4
  D_Flip_Flop d_ff_1 (.clk(CK), .D(controlled_buffer_3_out), .Q(d_ff_1_q));  // open: Qn, preset, en, reset
  D_Flip_Flop d_ff_2 (.clk(CK), .D(controlled_buffer_4_out), .Q(d_ff_2_q));  // open: Qn, preset, en, reset
  D_Flip_Flop d_ff_3 (.clk(CK), .D(controlled_buffer_1_out), .Q(d_ff_3_q));  // open: Qn, preset, en, reset
  D_Flip_Flop d_ff_4 (.clk(CK), .D(controlled_buffer_2_out), .Q(d_ff_4_q));  // open: Qn, preset, en, reset
  assign X[0] = r_2 ? d_ff_1_q : 1'bz;  // Controlled_Buffer controlled_buffer_5
  assign X[1] = r_2 ? d_ff_2_q : 1'bz;  // Controlled_Buffer controlled_buffer_6
  assign X[2] = r_2 ? d_ff_3_q : 1'bz;  // Controlled_Buffer controlled_buffer_7
  assign X[3] = r_2 ? d_ff_4_q : 1'bz;  // Controlled_Buffer controlled_buffer_8
  assign Y[0] = r2 ? d_ff_1_q : 1'bz;  // Controlled_Buffer controlled_buffer_9
  assign Y[1] = r2 ? d_ff_2_q : 1'bz;  // Controlled_Buffer controlled_buffer_10
  assign Y[2] = r2 ? d_ff_3_q : 1'bz;  // Controlled_Buffer controlled_buffer_11
  assign Y[3] = r2 ? d_ff_4_q : 1'bz;  // Controlled_Buffer controlled_buffer_12
endmodule

module Register_File (
  input  EXT1,
  input  EXT2,
  input  [3:0] data,
  input  wA,
  input  wB,
  input  wC,
  input  wD,
  input  r1A,
  input  r1B,
  input  r1C,
  input  r1D,
  input  r2A,
  input  r2B,
  input  r2C,
  input  r2D,
  input  CLK,
  output [3:0] Bus_X,
  output [3:0] Bus_Y,
  output [3:0] RD_out
);

  _4bitsRegister u_4bitsregister_1 (.R(data), .Y(Bus_Y), .X(Bus_X), .w(wA), .CK(CLK), .r_2(r1A), .r2(r2A));
  _4bitsRegister u_4bitsregister_2 (.R(data), .Y(Bus_Y), .X(Bus_X), .w(wB), .CK(CLK), .r_2(r1B), .r2(r2B));
  _4bitsRegister u_4bitsregister_3 (.R(data), .Y(Bus_Y), .X(Bus_X), .w(wC), .CK(CLK), .r_2(r1C), .r2(r2C));
  _4bitsRegister u_4bitsregister_4 (.R(data), .Y(Bus_Y), .X(Bus_X), .w(wD), .CK(CLK), .r_2(r1D), .r2(r2D));
  Pull_Resistor pull_resistor_1 (.node(Bus_X));
  Pull_Resistor pull_resistor_2 (.node(Bus_Y));
  Pull_Resistor pull_resistor_3 (.node(Bus_X));

  assign RD_out = Bus_X;

  // Other names for the same wires on the sheet: R[3:0] = data; X[3:0] = Bus_X; Y[3:0] = Bus_Y

  // Notes on the sheet:
  //   A
  //   B
  //   C
  //   D
endmodule

module Instruction_Register (
  input  [11:0] LOAD,
  input  w,
  input  r,
  input  CLK,
  output [11:0] S
);

  _4bitsRegister u_4bitsregister_1 (.R(LOAD[3:0]), .X(S[3:0]), .w(w), .CK(CLK), .r_2(r));  // open: Y, r2
  _4bitsRegister u_4bitsregister_2 (.R(LOAD[7:4]), .X(S[7:4]), .w(w), .CK(CLK), .r_2(r));  // open: Y, r2
  _4bitsRegister u_4bitsregister_3 (.R(LOAD[11:8]), .X(S[11:8]), .w(w), .CK(CLK), .r_2(r));  // open: Y, r2

  // Other names for the same wires on the sheet: A[3:0] = LOAD[3:0]; B[3:0] = LOAD[7:4]; C[3:0] = LOAD[11:8];
  //   _1[3:0] = S[3:0]; _2[3:0] = S[7:4]; _3[3:0] = S[11:8]
endmodule

module Adressing_Unit (
  input  in_1,
  input  in_2,
  input  ext1,
  input  ext2,
  input  PC0,
  input  PC1,
  input  PC2,
  input  PC3,
  input  AD0,
  input  AD1,
  input  AD2,
  input  AD3,
  input  CLK,
  output [3:0] PC_out,
  output [3:0] AD_out
);

  _4bitsRegister u_4bitsregister_1 (
    .R({PC3, PC2, PC1, PC0}), .Y(PC_out), .w(in_1), .CK(CLK), .r2(1'b1));  // open: X, r_2
  _4bitsRegister u_4bitsregister_2 (
    .R({AD3, AD2, AD1, AD0}), .Y(AD_out), .w(in_2), .CK(CLK), .r2(1'b1));  // open: X, r_2

  // Other names for the same wires on the sheet: W_AD = in_2; W_PC = in_1

  // Notes on the sheet:
  //   PC
  //   AD
endmodule

module Control_Unit (
  input  ext1,
  input  ext2,
  input  [11:0] in_3,
  input  [3:0] PC_in,
  input  CLK,
  input  RESET,
  output MEM_read,
  output MEM_write,
  output fetch,
  output wA,
  output wB,
  output wC,
  output wD,
  output r1A,
  output r1B,
  output r1C,
  output r1D,
  output r2A,
  output PC3,
  output PC2,
  output PC1,
  output PC0,
  output r2B,
  output wPC,
  output AD3,
  output AD2,
  output AD1,
  output AD0,
  output wAD,
  output r2C,
  output r2D,
  output f0,
  output f1,
  output f2
);

  wire _2, _3, and_7_out, and_8_out, and_17_out, CoDOp0, CodOp1, CodOp2, CodOp3, decoder_1_out1,
       decoder_1_out2, decoder_2_out0, decoder_2_out1, decoder_2_out2, decoder_2_out3, decoder_3_out0,
       decoder_3_out1, decoder_3_out2, decoder_3_out3, decoder_4_out0, decoder_4_out1, decoder_4_out2,
       decoder_4_out3, EXT0, EXT1_t, FORMAT, not_1_out, not_2_out, or_5_out, res0, res1, store, X0, X1,
       xor_1_out, Y0, Y1;
  wire [1:0] adder_2_out, multiplexer_4_out, register_1_q;
  wire [3:0] PC_plus;

  Adder #(.width(4)) adder_1 (.a(PC_in), .b(4'b0001), .out(PC_plus), .cin(1'b0));  // open: cout
  Instruction_Register instruction_register_1 (
    .LOAD(in_3), .w(fetch), .r(1'b1),
    .S({CodOp3, CodOp2, CodOp1, CoDOp0, res1, res0, X1, X0, Y1, Y0, EXT1_t, EXT0}), .CLK(CLK));
  Multiplexer #(.width(4)) multiplexer_1 (
    .in0(PC_plus), .in1(4'b0000), .out({PC3, PC2, PC1, PC0}), .sel(RESET));  // open: en
  or or_1 (wPC, RESET, _3);
  and and_1 (AD2, X0, wAD);
  and and_2 (AD3, X1, wAD);
  Register #(.width(2)) register_1 (.D(adder_2_out), .Q(register_1_q), .clk(CLK), .clr(RESET));  // open: en
  Adder #(.width(2)) adder_2 (.a(register_1_q), .b(2'b01), .out(adder_2_out));  // open: cin, cout
  and and_3 (AD1, Y1, wAD);
  and and_4 (AD0, Y0, wAD);
  and and_5 (MEM_read, ~CodOp3, CodOp2, ~CodOp1, ~CoDOp0);  // AND_Gate
  and and_6 (store, CodOp3, ~CodOp2, ~CodOp1, ~CoDOp0);  // AND_Gate
  Decoder #(.select(2)) decoder_1 (
    .out0(fetch), .out1(decoder_1_out1), .out2(decoder_1_out2), .out3(_3), .sel(register_1_q));  // open: en
  or or_2 (wAD, MEM_read, store);
  or or_3 (_2, decoder_1_out1, decoder_1_out2);
  Multiplexer multiplexer_2 (.in0(1'b0), .in1(store), .out(MEM_write), .sel(_3));  // open: en
  or or_4 (FORMAT, MEM_read, store);
  Multiplexer multiplexer_3 (.in0(X1), .in1(res1), .out(multiplexer_4_out[1]), .sel(store));  // open: en
  Multiplexer multiplexer_4 (.in0(X0), .in1(res0), .out(multiplexer_4_out[0]), .sel(store));  // open: en
  and and_7 (and_7_out, _2, or_5_out);
  Decoder #(.select(2)) decoder_2 (
    .out0(decoder_2_out0), .out1(decoder_2_out1), .out2(decoder_2_out2), .out3(decoder_2_out3),
    .sel({res1, res0}));  // open: en
  and and_8 (and_8_out, ~FORMAT, _2);  // AND_Gate
  Decoder #(.select(2)) decoder_3 (
    .out0(decoder_3_out0), .out1(decoder_3_out1), .out2(decoder_3_out2), .out3(decoder_3_out3),
    .sel(multiplexer_4_out));  // open: en
  Decoder #(.select(2)) decoder_4 (
    .out0(decoder_4_out0), .out1(decoder_4_out1), .out2(decoder_4_out2), .out3(decoder_4_out3), .sel({Y1, Y0}));  // open: en
  not not_1 (not_1_out, FORMAT);
  or or_5 (or_5_out, MEM_read, not_1_out);
  and and_9 (wA, and_7_out, decoder_2_out0);
  and and_10 (wB, and_7_out, decoder_2_out1);
  and and_11 (wC, and_7_out, decoder_2_out2);
  and and_12 (wD, and_7_out, decoder_2_out3);
  xor xor_1 (xor_1_out, and_8_out, store);
  and and_13 (r1A, xor_1_out, decoder_3_out0);
  and and_14 (r1B, xor_1_out, decoder_3_out1);
  and and_15 (r1C, xor_1_out, decoder_3_out2);
  and and_16 (r1D, xor_1_out, decoder_3_out3);
  not not_2 (not_2_out, FORMAT);
  and and_17 (and_17_out, _2, not_2_out);
  and and_18 (r2A, and_17_out, decoder_4_out0);
  and and_19 (r2B, and_17_out, decoder_4_out1);
  and and_20 (r2C, and_17_out, decoder_4_out2);
  and and_21 (r2D, and_17_out, decoder_4_out3);
  and and_22 (f0, and_17_out, CoDOp0);
  and and_23 (f1, and_17_out, CodOp1);
  and and_24 (f2, and_17_out, CodOp2);

  // Other names for the same wires on the sheet: _1 = fetch; AD_plus = MEM_read

  // Notes on the sheet:
  //   RESET PC
  //   SEQUENCER
  //   LOAD = 0100
  //   STORE = 1000
  //   STATES
  //   1: fetch
  //   3: Increase PC
  //   First detect the instruction format
  //   SEL 1= Immediat 0 = Registre
  //   2: Decode and Execute
  //   Decode using decoders
  //   and send the appropriate control signals
endmodule

module _4BitsAdder (
  input  Cin,
  input  [3:0] A,
  input  [3:0] B,
  output [3:0] S,
  output Cout
);

  wire full_adder_1_carry_out, full_adder_2_carry_out, full_adder_3_carry_out;

  Full_Adder full_adder_1 (.A(A[0]), .B(B[0]), .Sum(S[0]), .Carry_in(Cin), .Carry_out(full_adder_1_carry_out));
  Full_Adder full_adder_2 (
    .A(A[1]), .B(B[1]), .Sum(S[1]), .Carry_in(full_adder_1_carry_out), .Carry_out(full_adder_2_carry_out));
  Full_Adder full_adder_3 (
    .A(A[2]), .B(B[2]), .Sum(S[2]), .Carry_in(full_adder_2_carry_out), .Carry_out(full_adder_3_carry_out));
  Full_Adder full_adder_4 (.A(A[3]), .B(B[3]), .Sum(S[3]), .Carry_in(full_adder_3_carry_out), .Carry_out(Cout));
endmodule

module CPU (
  input  [3:0] DATA_in,
  input  CLK,
  input  [11:0] RI_in,
  input  RESET,
  input  ext1,
  input  ext2,
  output [3:0] DATA_out,
  output fetch,
  output MEM_read,
  output MEM_write,
  output [3:0] AD_out,
  output [3:0] PC_out
);

  wire control_unit_1_ad0, control_unit_1_ad1, control_unit_1_ad2, control_unit_1_ad3, control_unit_1_pc0,
       control_unit_1_pc1, control_unit_1_pc2, control_unit_1_pc3, control_unit_1_r1a, control_unit_1_r1b,
       control_unit_1_r1c, control_unit_1_r1d, control_unit_1_r2a, control_unit_1_r2b, control_unit_1_r2c,
       control_unit_1_r2d, control_unit_1_wa, control_unit_1_wad, control_unit_1_wb, control_unit_1_wc,
       control_unit_1_wd, control_unit_1_wpc, f0, f1, f2, n7segdisplay_selector_1_a,
       n7segdisplay_selector_1_b, n7segdisplay_selector_1_c, n7segdisplay_selector_1_d,
       n7segdisplay_selector_1_e, n7segdisplay_selector_1_f, n7segdisplay_selector_1_g,
       n7segdisplay_selector_2_a, n7segdisplay_selector_2_b, n7segdisplay_selector_2_c,
       n7segdisplay_selector_2_d, n7segdisplay_selector_2_e, n7segdisplay_selector_2_f,
       n7segdisplay_selector_2_g, n7segdisplay_selector_3_a, n7segdisplay_selector_3_b,
       n7segdisplay_selector_3_c, n7segdisplay_selector_3_d, n7segdisplay_selector_3_e,
       n7segdisplay_selector_3_f, n7segdisplay_selector_3_g;
  wire [3:0] multiplexer_1_out, n4bits_alu_1_s, register_file_1_bus_y;

  Control_Unit control_unit_1 (
    .in_3(RI_in), .PC_in(PC_out), .CLK(CLK), .wA(control_unit_1_wa), .wB(control_unit_1_wb),
    .wC(control_unit_1_wc), .wD(control_unit_1_wd), .r1A(control_unit_1_r1a), .r1B(control_unit_1_r1b),
    .r1C(control_unit_1_r1c), .r1D(control_unit_1_r1d), .r2A(control_unit_1_r2a), .r2B(control_unit_1_r2b),
    .r2C(control_unit_1_r2c), .r2D(control_unit_1_r2d), .f0(f0), .f1(f1), .f2(f2), .MEM_read(MEM_read),
    .MEM_write(MEM_write), .PC3(control_unit_1_pc3), .PC2(control_unit_1_pc2), .PC1(control_unit_1_pc1),
    .PC0(control_unit_1_pc0), .wPC(control_unit_1_wpc), .AD3(control_unit_1_ad3), .AD2(control_unit_1_ad2),
    .AD1(control_unit_1_ad1), .AD0(control_unit_1_ad0), .wAD(control_unit_1_wad), .RESET(RESET), .fetch(fetch));  // open: ext1, ext2
  _7_Segment_Display u_7_segment_display_1 (
    .g(n7segdisplay_selector_1_g), .f(n7segdisplay_selector_1_f), .a(n7segdisplay_selector_1_a),
    .b(n7segdisplay_selector_1_b), .e(n7segdisplay_selector_1_e), .d(n7segdisplay_selector_1_d),
    .c(n7segdisplay_selector_1_c));  // open: dp
  _7SegDisplay_Selector u_7segdisplay_selector_1 (
    .in_1(AD_out), .a(n7segdisplay_selector_1_a), .b(n7segdisplay_selector_1_b),
    .c(n7segdisplay_selector_1_c), .d(n7segdisplay_selector_1_d), .e(n7segdisplay_selector_1_e),
    .f(n7segdisplay_selector_1_f), .g(n7segdisplay_selector_1_g));
  Multiplexer #(.width(4)) multiplexer_1 (
    .in0(n4bits_alu_1_s), .in1(DATA_in), .out(multiplexer_1_out), .sel(MEM_read));  // open: en
  Adressing_Unit adressing_unit_1 (
    .PC_out(PC_out), .AD_out(AD_out), .in_1(control_unit_1_wpc), .in_2(control_unit_1_wad), .CLK(CLK),
    .PC1(control_unit_1_pc1), .PC2(control_unit_1_pc2), .PC3(control_unit_1_pc3), .PC0(control_unit_1_pc0),
    .AD0(control_unit_1_ad0), .AD1(control_unit_1_ad1), .AD2(control_unit_1_ad2), .AD3(control_unit_1_ad3));  // open: ext1, ext2
  Register_File register_file_1 (
    .wA(control_unit_1_wa), .wB(control_unit_1_wb), .wC(control_unit_1_wc), .wD(control_unit_1_wd),
    .r1A(control_unit_1_r1a), .r1B(control_unit_1_r1b), .r1C(control_unit_1_r1c), .r1D(control_unit_1_r1d),
    .r2A(control_unit_1_r2a), .r2B(control_unit_1_r2b), .r2C(control_unit_1_r2c), .r2D(control_unit_1_r2d),
    .Bus_X(DATA_out), .Bus_Y(register_file_1_bus_y), .data(multiplexer_1_out), .CLK(CLK));  // open: EXT1, EXT2, RD_out
  _7_Segment_Display u_7_segment_display_2 (
    .g(n7segdisplay_selector_2_g), .f(n7segdisplay_selector_2_f), .a(n7segdisplay_selector_2_a),
    .b(n7segdisplay_selector_2_b), .e(n7segdisplay_selector_2_e), .d(n7segdisplay_selector_2_d),
    .c(n7segdisplay_selector_2_c));  // open: dp
  _7SegDisplay_Selector u_7segdisplay_selector_2 (
    .in_1(PC_out), .a(n7segdisplay_selector_2_a), .b(n7segdisplay_selector_2_b),
    .c(n7segdisplay_selector_2_c), .d(n7segdisplay_selector_2_d), .e(n7segdisplay_selector_2_e),
    .f(n7segdisplay_selector_2_f), .g(n7segdisplay_selector_2_g));
  _4bits_ALU u_4bits_alu_1 (
    .F2(f2), .F1(f1), .in_3(f0), .A(DATA_out), .B(register_file_1_bus_y), .S(n4bits_alu_1_s));  // open: ext1, ext2, out_8
  _7SegDisplay_Selector u_7segdisplay_selector_3 (
    .in_1(n4bits_alu_1_s), .a(n7segdisplay_selector_3_a), .b(n7segdisplay_selector_3_b),
    .c(n7segdisplay_selector_3_c), .d(n7segdisplay_selector_3_d), .e(n7segdisplay_selector_3_e),
    .f(n7segdisplay_selector_3_f), .g(n7segdisplay_selector_3_g));
  _7_Segment_Display u_7_segment_display_3 (
    .g(n7segdisplay_selector_3_g), .f(n7segdisplay_selector_3_f), .a(n7segdisplay_selector_3_a),
    .b(n7segdisplay_selector_3_b), .e(n7segdisplay_selector_3_e), .d(n7segdisplay_selector_3_d),
    .c(n7segdisplay_selector_3_c));  // open: dp
endmodule

// e
module _7SegDisplay_Selector (
  input  [3:0] in_1,
  output a,
  output b,
  output c,
  output d,
  output e,
  output f,
  output g
);

  wire decoder_1_out0, decoder_1_out1, decoder_1_out2, decoder_1_out3, decoder_1_out4, decoder_1_out5,
       decoder_1_out6, decoder_1_out7, decoder_1_out8, decoder_1_out9, decoder_1_out10, decoder_1_out11,
       decoder_1_out12, decoder_1_out13, decoder_1_out14, decoder_1_out15;

  Decoder #(.select(4)) decoder_1 (
    .out0(decoder_1_out0), .out1(decoder_1_out1), .out2(decoder_1_out2), .out3(decoder_1_out3),
    .out4(decoder_1_out4), .out5(decoder_1_out5), .out6(decoder_1_out6), .out7(decoder_1_out7),
    .out8(decoder_1_out8), .out9(decoder_1_out9), .out10(decoder_1_out10), .out11(decoder_1_out11),
    .out12(decoder_1_out12), .out13(decoder_1_out13), .out14(decoder_1_out14), .out15(decoder_1_out15),
    .sel(in_1));  // open: en
  or or_1 (a, decoder_1_out0, decoder_1_out2, decoder_1_out3, decoder_1_out5, decoder_1_out6, decoder_1_out7, decoder_1_out8, decoder_1_out9, decoder_1_out10, decoder_1_out12, decoder_1_out14, decoder_1_out15);
  or or_2 (b, decoder_1_out0, decoder_1_out1, decoder_1_out2, decoder_1_out3, decoder_1_out4, decoder_1_out7, decoder_1_out8, decoder_1_out9, decoder_1_out10, decoder_1_out13);
  or or_3 (c, decoder_1_out0, decoder_1_out1, decoder_1_out3, decoder_1_out4, decoder_1_out5, decoder_1_out6, decoder_1_out7, decoder_1_out8, decoder_1_out9, decoder_1_out10, decoder_1_out11, decoder_1_out13);
  or or_4 (d, decoder_1_out0, decoder_1_out2, decoder_1_out3, decoder_1_out5, decoder_1_out6, decoder_1_out8, decoder_1_out11, decoder_1_out12, decoder_1_out13, decoder_1_out14);
  or or_5 (e, decoder_1_out0, decoder_1_out2, decoder_1_out6, decoder_1_out8, decoder_1_out10, decoder_1_out11, decoder_1_out12, decoder_1_out13, decoder_1_out14, decoder_1_out15);
  or or_6 (f, decoder_1_out0, decoder_1_out4, decoder_1_out5, decoder_1_out6, decoder_1_out8, decoder_1_out9, decoder_1_out10, decoder_1_out11, decoder_1_out12, decoder_1_out14, decoder_1_out15);
  or or_7 (g, decoder_1_out2, decoder_1_out3, decoder_1_out4, decoder_1_out5, decoder_1_out6, decoder_1_out8, decoder_1_out9, decoder_1_out10, decoder_1_out11, decoder_1_out13, decoder_1_out14, decoder_1_out15);
endmodule
